// Logisim project Cpu (1).circ as structural Verilog: 19 circuits, main circuit main
module main (
  input  [19:0] in_1,
  input  in_2,
  output [19:0] out_3,
  output [19:0] out_4,
  output [19:0] out_5,
  output [3:0] out_6,
  output [3:0] out_7,
  output [19:0] out_8,
  output [3:0] out_9,
  output [19:0] out_10,
  output [3:0] out_11
);

  wire and_2_out, and_3_out, and_4_out, and_6_out, CLCK, \IMM_Sıgnal , is_ADD_SUB, is_ALU, is_AND, is_BE,
       is_BNE, is_BNE_BE, is_eq, is_JUMP, is_OR, is_POP, is_PUSH, is_SUB, is_XOR, Mem_Read, Mem_Write,
       not_1_out, or_2_out, or_3_out, or_4_out, or_5_out, programcounter_1_p1, programcounter_1_p2,
       Write_Enable;
  wire [1:1] and_1_out, and_5_out;
  wire [3:0] Dest_ST_SRC, Reg1, Reg2, SRC1, SRC2;
  wire [9:0] ADDRESS_LD_STD;
  wire [15:0] SRC1_PUSH_POP;
  wire [19:0] ADDRESS_JUMP_BE, ALU_Result, Data_Out, IMM_Value, programcounter_1_p4, rom_1_data;

  Multiplexer #(.width(20), .enable("false")) multiplexer_1 (
    .in0(Data_Out), .in1(ALU_Result), .out(out_3), .sel(is_ALU));
  // ProgramCounter programcounter_1: pin names not known; wires that end beside it: programcounter_1_p1, programcounter_1_p2, in_2, programcounter_1_p4
  or or_1 (programcounter_1_p1, is_JUMP, is_BNE_BE);
  Clock clock_1 (.out(CLCK));
  Register_File register_file_1 (
    .Input_data(out_3), .write_source__register(Dest_ST_SRC), .Write_Enable(Write_Enable), .clck(CLCK),
    .clear(in_2), .Input_Reg1(out_6), .Input_Reg2(out_7), .Register_1_Data(out_8), .Register_2_Data(out_5));
  and and_1 (and_1_out[1], is_BNE_BE, or_2_out);
  ROM #(.addrWidth(20), .dataWidth(20)) rom_1 (.addr(programcounter_1_p4), .data(rom_1_data), .sel(1'b1));
  Multiplexer #(.select(2), .width(20), .enable("false")) multiplexer_2 (
    .in0(20'h1), .in1(ADDRESS_JUMP_BE), .in2(ADDRESS_JUMP_BE), .out(out_10), .sel({and_1_out[1], is_JUMP}));  // open: in3
  and and_2 (and_2_out, is_BE, is_eq);
  _20_Bit_Comparator u_20_bit_comparator_1 (.in_1(out_8), .in_2(out_5), .eq(is_eq));
  or or_2 (or_2_out, and_2_out, and_3_out);
  and and_3 (and_3_out, not_1_out, is_BNE);
  not not_1 (not_1_out, is_eq);
  CPU cpu_1 (
    .Assembly(in_1), .DEST___ST_SRC(Dest_ST_SRC), .IMM_SIGNAL(\IMM_Sıgnal ), .SRC1(SRC1), .SRC2(SRC2),
    .is_ADD_SUB(is_ADD_SUB), .is_OR(is_OR), .is_XOR(is_XOR), .is_AND(is_AND), .is_SUB_2(is_SUB),
    .is_Push(is_PUSH), .is_Pop(is_POP), .is_Jump(is_JUMP), .Mem_Write(Mem_Write), .Mem_Read(Mem_Read),
    .SRC1_PUSH_POP(SRC1_PUSH_POP), .REG1(Reg1), .REG2(Reg2), .IMM(IMM_Value), .is_SUB(is_SUB),
    .is_ALU(is_ALU), .Mem_Write_Enabled(Write_Enable), .ADDRESS_LD_ST(ADDRESS_LD_STD),
    .ADDRESS_JUMP_BE_BNE(ADDRESS_JUMP_BE), .is_BE(is_BE), .is_BNE(is_BNE), .is_BNE_BE(is_BNE_BE));
  ALU alu_1 (
    .Outpu(ALU_Result), .A(out_8), .B(out_4), .is_Sub(is_SUB), .is_XOR(is_XOR), .is_OR(is_OR),
    .is_AND(is_AND), .is_ADD_SUB(is_ADD_SUB));  // open: c_Out
  or or_3 (or_3_out, is_BE, is_BNE);
  or or_4 (or_4_out, is_BE, is_BNE);
  and and_4 (and_4_out, or_3_out, is_BNE_BE);
  or or_5 (or_5_out, is_ADD_SUB, is_OR, is_AND, is_XOR);
  RAM #(.addrWidth(10), .dataWidth(20), .bus("separate")) ram_1 (
    .addr(ADDRESS_LD_STD), .din(out_8), .data(Data_Out), .str(Mem_Write), .sel(1'b1), .clk(CLCK),
    .ld(Mem_Read), .clr(1'b0));
  and and_5 (and_5_out[1], or_4_out, is_BNE_BE);
  Multiplexer #(.width(4), .enable("false")) multiplexer_3 (.in0(SRC2), .in1(Reg2), .out(out_7), .sel(and_4_out));
  Multiplexer #(.width(20), .enable("false")) multiplexer_4 (
    .in0(out_5), .in1(IMM_Value), .out(out_4), .sel(and_6_out));
  and and_6 (and_6_out, or_5_out, \IMM_Sıgnal );
  Multiplexer #(.select(2), .width(4), .enable("false")) multiplexer_5 (
    .in0(SRC1), .in1(Dest_ST_SRC), .in2(Reg1), .out(out_6), .sel({and_5_out[1], Mem_Write}));  // open: in3

  assign out_9 = out_6;
  assign out_11 = out_7;

  // Other names for the same wires on the sheet: ALU_Second_Input[19:0] = out_4; Clear = in_2; input[19:0] = out_10;
  //   reg1_value[19:0] = out_8; reg2_value[19:0] = out_5; Register1[3:0] = out_6; Register2[3:0] = out_7

  // Notes on the sheet:
  //   Next İnstruction sanırım fsm lerden sonra yapılıcak
  //   contents of rom_1 (hex, n*v repeats v):
  //   4000 4202 8440 8683 c60a 86ec 2801 2063 a000
endmodule

module half_adder (
  input  A,
  input  B,
  output sum,
  output c_out
);

  xor xor_1 (sum, A, B);
  and and_1 (c_out, A, B);
endmodule

module Full_Adder (
  input  C_in,
  input  A,
  input  B,
  output Sum,
  output C_Out
);

  wire half_adder_1_c_out, half_adder_2_c_out, half_adder_2_sum;

  half_adder half_adder_1 (.A(C_in), .B(half_adder_2_sum), .sum(Sum), .c_out(half_adder_1_c_out));
  half_adder half_adder_2 (.A(A), .B(B), .sum(half_adder_2_sum), .c_out(half_adder_2_c_out));
  or or_1 (C_Out, half_adder_1_c_out, half_adder_2_c_out);
endmodule

module _2_Bit_Adder (
  input  [1:0] A,
  input  [1:0] B,
  input  C_in,
  output [1:0] sum,
  output C_Out
);

  wire full_adder_1_c_out;

  Full_Adder full_adder_1 (.C_in(B[0]), .A(A[0]), .B(C_in), .Sum(sum[0]), .C_Out(full_adder_1_c_out));
  Full_Adder full_adder_2 (.C_in(full_adder_1_c_out), .A(A[1]), .B(B[1]), .Sum(sum[1]), .C_Out(C_Out));
endmodule

module _4_Bit_Adder (
  input  [3:0] A,
  input  [3:0] B,
  input  in_3,
  output [3:0] sum,
  output c_out
);

  wire n2_bit_adder_1_c_out;

  _2_Bit_Adder u_2_bit_adder_1 (.C_in(in_3), .A(A[1:0]), .B(B[1:0]), .sum(sum[1:0]), .C_Out(n2_bit_adder_1_c_out));
  _2_Bit_Adder u_2_bit_adder_2 (.C_in(n2_bit_adder_1_c_out), .A(A[3:2]), .B(B[3:2]), .sum(sum[3:2]), .C_Out(c_out));
endmodule

module _4_Bit_Half_Adder (
  input  [3:0] A,
  input  [3:0] B,
  output [3:0] sum,
  output C_Out
);

  wire full_adder_1_c_out, full_adder_2_c_out, half_adder_1_c_out;

  half_adder half_adder_1 (.A(A[0]), .B(B[0]), .sum(sum[0]), .c_out(half_adder_1_c_out));
  Full_Adder full_adder_1 (.C_in(half_adder_1_c_out), .A(A[1]), .B(B[1]), .Sum(sum[1]), .C_Out(full_adder_1_c_out));
  Full_Adder full_adder_2 (.C_in(full_adder_1_c_out), .A(A[2]), .B(B[2]), .Sum(sum[2]), .C_Out(full_adder_2_c_out));
  Full_Adder full_adder_3 (.C_in(full_adder_2_c_out), .A(A[3]), .B(B[3]), .Sum(sum[3]), .C_Out(C_Out));
endmodule

module _8_Bit_Adder (
  input  [7:0] A,
  input  [7:0] B,
  input  c_in,
  output [7:0] sum,
  output c_out
);

  wire n4_bit_adder_1_c_out;

  _4_Bit_Adder u_4_bit_adder_1 (.in_3(c_in), .A(A[3:0]), .B(B[3:0]), .sum(sum[3:0]), .c_out(n4_bit_adder_1_c_out));
  _4_Bit_Adder u_4_bit_adder_2 (.in_3(n4_bit_adder_1_c_out), .A(A[7:4]), .B(B[7:4]), .sum(sum[7:4]), .c_out(c_out));
endmodule

module _16_Bit_Adder (
  input  [15:0] A,
  input  [15:0] B,
  input  c_in,
  output [15:0] sum,
  output c_out
);

  wire n8_bit_adder_1_c_out;

  _8_Bit_Adder u_8_bit_adder_1 (.c_in(c_in), .A(A[7:0]), .B(B[7:0]), .sum(sum[7:0]), .c_out(n8_bit_adder_1_c_out));
  _8_Bit_Adder u_8_bit_adder_2 (.c_in(n8_bit_adder_1_c_out), .A(A[15:8]), .B(B[15:8]), .sum(sum[15:8]), .c_out(c_out));
endmodule

module _20_Bit_Adder (
  input  [19:0] A,
  input  [19:0] B,
  input  C_in,
  output [19:0] Sum,
  output C_Out
);

  wire n4_bit_adder_1_c_out;

  _4_Bit_Adder u_4_bit_adder_1 (.in_3(C_in), .A(A[3:0]), .B(B[3:0]), .sum(Sum[3:0]), .c_out(n4_bit_adder_1_c_out));
  _16_Bit_Adder u_16_bit_adder_1 (
    .c_in(n4_bit_adder_1_c_out), .A(A[19:4]), .B(B[19:4]), .sum(Sum[19:4]), .c_out(C_Out));
endmodule

module ALU (
  input  is_Sub,
  input  [19:0] A,
  input  [19:0] B,
  input  is_XOR,
  input  is_OR,
  input  is_AND,
  input  is_ADD_SUB,
  output c_Out,
  output [19:0] Outpu
);

  wire [19:0] and_1_out, multiplexer_1_out, n20_bit_adder_1_sum, not_1_out, or_1_out, xor_1_out;

  assign not_1_out = ~B;  // NOT_Gate not_1, 20 bits wide
  Multiplexer #(.width(20), .enable("false")) multiplexer_1 (
    .in0(B), .in1(not_1_out), .out(multiplexer_1_out), .sel(is_Sub));
  assign and_1_out = B & A;  // AND_Gate and_1, 20 bits wide
  assign or_1_out = B | A;  // OR_Gate or_1, 20 bits wide
  assign xor_1_out = B ^ A;  // XOR_Gate xor_1, 20 bits wide
  _20_Bit_Adder u_20_bit_adder_1 (
    .C_in(is_Sub), .A(A), .B(multiplexer_1_out), .Sum(n20_bit_adder_1_sum), .C_Out(c_Out));
  assign Outpu = is_XOR ? xor_1_out : 20'bz;  // Controlled_Buffer controlled_buffer_1
  assign Outpu = is_AND ? and_1_out : 20'bz;  // Controlled_Buffer controlled_buffer_2
  assign Outpu = is_OR ? or_1_out : 20'bz;  // Controlled_Buffer controlled_buffer_3
  assign Outpu = is_ADD_SUB ? n20_bit_adder_1_sum : 20'bz;  // Controlled_Buffer controlled_buffer_4
endmodule

module CPU (
  input  [19:0] Assembly,
  output [3:0] REG1,
  output [3:0] DEST___ST_SRC,
  output [3:0] REG2,
  output IMM_SIGNAL,
  output Mem_Read,
  output [3:0] SRC1,
  output Mem_Write,
  output is_Jump,
  output [3:0] SRC2,
  output is_Push,
  output is_Pop,
  output is_BNE_BE,
  output is_SUB,
  output is_BE,
  output is_BNE,
  output is_ADD_SUB,
  output is_OR,
  output is_XOR,
  output is_AND,
  output [15:0] SRC1_PUSH_POP,
  output is_SUB_2,
  output [19:0] IMM,
  output is_ALU,
  output [9:0] ADDRESS_LD_ST,
  output Mem_Write_Enabled,
  output [19:0] ADDRESS_JUMP_BE_BNE
);

  wire ADD, ADDI, AND, ANDI, OR, or_1_out, ORI, SUB, SUBI, XOR, XORI;
  wire [9:0] bit_extender_2_out;
  wire [19:0] bit_extender_3_out, bit_extender_4_out;

  assign IMM = {{12{1'b0}}, Assembly[7:0]};  // Bit_Extender bit_extender_1
  Bit_Extender #(.in_width(12), .out_width(10)) bit_extender_2 (
    .in({Assembly[0], Assembly[1], Assembly[2], Assembly[3], Assembly[4], Assembly[5], Assembly[6], Assembly[7], Assembly[8], Assembly[9], Assembly[10], Assembly[11]}),
    .out(bit_extender_2_out));
  assign bit_extender_3_out = {{14{1'b0}}, Assembly[5:0]};  // Bit_Extender bit_extender_3
  assign bit_extender_4_out = {{4{1'b0}}, Assembly[15:0]};  // Bit_Extender bit_extender_4
  assign ADDRESS_LD_ST = or_1_out ? bit_extender_2_out : 10'bz;  // Controlled_Buffer controlled_buffer_1
  assign ADDRESS_JUMP_BE_BNE = is_BNE_BE ? bit_extender_3_out : 20'bz;  // Controlled_Buffer controlled_buffer_2
  assign ADDRESS_JUMP_BE_BNE = is_Jump ? bit_extender_4_out : 20'bz;  // Controlled_Buffer controlled_buffer_3
  or or_1 (or_1_out, Mem_Write, Mem_Read);
  or or_2 (Mem_Write_Enabled, is_ALU, Mem_Read);
  not not_1 (is_BE, Assembly[14]);
  Decoder #(.select(4), .enable("false")) decoder_1 (
    .out0(SUB), .out1(ADD), .out2(AND), .out3(OR), .out4(XOR), .out5(ADDI), .out6(SUBI), .out7(ANDI),
    .out8(ORI), .out9(XORI), .out10(Mem_Read), .out11(Mem_Write), .out12(is_Jump), .out13(is_Push),
    .out14(is_Pop), .out15(is_BNE_BE), .sel(Assembly[19:16]));
  or or_3 (is_SUB, SUB, SUBI);
  or or_4 (is_ADD_SUB, ADD, SUB, SUBI, ADDI);
  or or_5 (is_OR, OR, ORI);
  or or_6 (is_XOR, XOR, XORI);
  or or_7 (is_AND, AND, ANDI);
  or or_8 (is_SUB_2, SUB, ORI);
  or or_9 (IMM_SIGNAL, ADDI, SUBI, ANDI, ORI, XORI);
  or or_10 (is_ALU, is_XOR, is_ADD_SUB, is_SUB, is_OR, is_SUB_2);

  assign DEST___ST_SRC = Assembly[15:12];
  assign is_BNE = Assembly[14];
  assign REG1 = Assembly[13:10];
  assign REG2 = Assembly[9:6];
  assign SRC1 = Assembly[11:8];
  assign SRC1_PUSH_POP = Assembly[15:0];
  assign SRC2 = Assembly[3:0];

  // Other names for the same wires on the sheet: ADDR_BE_BNE[5:0] = Assembly[5:0];
  //   ADDRESS_JUMP[15:0] = Assembly[15:0];
  //   ADDRESS_LD_ST_t[11:0] = {Assembly[0], Assembly[1], Assembly[2], Assembly[3], Assembly[4], Assembly[5], Assembly[6], Assembly[7], Assembly[8], Assembly[9], Assembly[10], Assembly[11]};
  //   IMM_t[7:0] = Assembly[7:0]; SRC1__PUSH_POP[15:0] = Assembly[15:0]; BE_BNE = is_BNE_BE; is_LD = Mem_Read;
  //   is_ST = Mem_Write; OPCODE[3:0] = Assembly[19:16]; DST[3:0] = Assembly[15:12]; ST_SRC[3:0] = Assembly[15:12]
endmodule

module _20_Bit_Register (
  input  [19:0] Input,
  input  in_2,
  input  enable,
  input  clear,
  input  clk,
  output [19:0] out_6
);

  wire multiplexer_1_out, multiplexer_2_out, multiplexer_3_out, multiplexer_4_out, multiplexer_5_out,
       multiplexer_6_out, multiplexer_7_out, multiplexer_8_out, multiplexer_9_out, multiplexer_10_out,
       multiplexer_11_out, multiplexer_12_out, multiplexer_13_out, multiplexer_14_out, multiplexer_15_out,
       multiplexer_16_out, multiplexer_17_out, multiplexer_18_out, multiplexer_19_out, multiplexer_20_out;
  wire [0:0] not_1_out;

  not not_1 (not_1_out[0], enable);
  Multiplexer #(.select(2), .enable("false")) multiplexer_1 (
    .in0(Input[19]), .in1(out_6[19]), .in2(in_2), .in3(in_2), .out(multiplexer_1_out),
    .sel({clear, not_1_out[0]}));
  Multiplexer #(.select(2), .enable("false")) multiplexer_2 (
    .in0(Input[18]), .in1(out_6[18]), .in2(in_2), .in3(in_2), .out(multiplexer_2_out),
    .sel({clear, not_1_out[0]}));
  d_flip_flop d_flip_flop_1 (.D(multiplexer_1_out), .clk(clk), .Q(out_6[19]));
  Multiplexer #(.select(2), .enable("false")) multiplexer_3 (
    .in0(Input[17]), .in1(out_6[17]), .in2(in_2), .in3(in_2), .out(multiplexer_3_out),
    .sel({clear, not_1_out[0]}));
  d_flip_flop d_flip_flop_2 (.D(multiplexer_2_out), .clk(clk), .Q(out_6[18]));
  Multiplexer #(.select(2), .enable("false")) multiplexer_4 (
    .in0(Input[16]), .in1(out_6[16]), .in2(in_2), .in3(in_2), .out(multiplexer_4_out),
    .sel({clear, not_1_out[0]}));
  d_flip_flop d_flip_flop_3 (.D(multiplexer_3_out), .clk(clk), .Q(out_6[17]));
  Multiplexer #(.select(2), .enable("false")) multiplexer_5 (
    .in0(Input[15]), .in1(out_6[15]), .in2(in_2), .in3(in_2), .out(multiplexer_5_out),
    .sel({clear, not_1_out[0]}));
  d_flip_flop d_flip_flop_4 (.D(multiplexer_4_out), .clk(clk), .Q(out_6[16]));
  Multiplexer #(.select(2), .enable("false")) multiplexer_6 (
    .in0(Input[14]), .in1(out_6[14]), .in2(in_2), .in3(in_2), .out(multiplexer_6_out),
    .sel({clear, not_1_out[0]}));
  d_flip_flop d_flip_flop_5 (.D(multiplexer_5_out), .clk(clk), .Q(out_6[15]));
  Multiplexer #(.select(2), .enable("false")) multiplexer_7 (
    .in0(Input[13]), .in1(out_6[13]), .in2(in_2), .in3(in_2), .out(multiplexer_7_out),
    .sel({clear, not_1_out[0]}));
  d_flip_flop d_flip_flop_6 (.D(multiplexer_6_out), .clk(clk), .Q(out_6[14]));
  Multiplexer #(.select(2), .enable("false")) multiplexer_8 (
    .in0(Input[12]), .in1(out_6[12]), .in2(in_2), .in3(in_2), .out(multiplexer_8_out),
    .sel({clear, not_1_out[0]}));
  d_flip_flop d_flip_flop_7 (.D(multiplexer_7_out), .clk(clk), .Q(out_6[13]));
  Multiplexer #(.select(2), .enable("false")) multiplexer_9 (
    .in0(Input[11]), .in1(out_6[11]), .in2(in_2), .in3(in_2), .out(multiplexer_9_out),
    .sel({clear, not_1_out[0]}));
  d_flip_flop d_flip_flop_8 (.D(multiplexer_8_out), .clk(clk), .Q(out_6[12]));
  Multiplexer #(.select(2), .enable("false")) multiplexer_10 (
    .in0(Input[10]), .in1(out_6[10]), .in2(in_2), .in3(in_2), .out(multiplexer_10_out),
    .sel({clear, not_1_out[0]}));
  d_flip_flop d_flip_flop_9 (.D(multiplexer_9_out), .clk(clk), .Q(out_6[11]));
  Multiplexer #(.select(2), .enable("false")) multiplexer_11 (
    .in0(Input[9]), .in1(out_6[9]), .in2(in_2), .in3(in_2), .out(multiplexer_11_out),
    .sel({clear, not_1_out[0]}));
  d_flip_flop d_flip_flop_10 (.D(multiplexer_10_out), .clk(clk), .Q(out_6[10]));
  Multiplexer #(.select(2), .enable("false")) multiplexer_12 (
    .in0(Input[8]), .in1(out_6[8]), .in2(in_2), .in3(in_2), .out(multiplexer_12_out),
    .sel({clear, not_1_out[0]}));
  d_flip_flop d_flip_flop_11 (.D(multiplexer_11_out), .clk(clk), .Q(out_6[9]));
  Multiplexer #(.select(2), .enable("false")) multiplexer_13 (
    .in0(Input[7]), .in1(out_6[6]), .in2(in_2), .in3(in_2), .out(multiplexer_13_out),
    .sel({clear, not_1_out[0]}));
  d_flip_flop d_flip_flop_12 (.D(multiplexer_12_out), .clk(clk), .Q(out_6[8]));
  Multiplexer #(.select(2), .enable("false")) multiplexer_14 (
    .in0(Input[6]), .in1(out_6[5]), .in2(in_2), .in3(in_2), .out(multiplexer_14_out),
    .sel({clear, not_1_out[0]}));
  d_flip_flop d_flip_flop_13 (.D(multiplexer_13_out), .clk(clk), .Q(out_6[6]));
  Multiplexer #(.select(2), .enable("false")) multiplexer_15 (
    .in0(Input[5]), .in1(out_6[4]), .in2(in_2), .in3(in_2), .out(multiplexer_15_out),
    .sel({clear, not_1_out[0]}));
  d_flip_flop d_flip_flop_14 (.D(multiplexer_14_out), .clk(clk), .Q(out_6[5]));
  Multiplexer #(.select(2), .enable("false")) multiplexer_16 (
    .in0(Input[4]), .in1(out_6[7]), .in2(in_2), .in3(in_2), .out(multiplexer_16_out),
    .sel({clear, not_1_out[0]}));
  d_flip_flop d_flip_flop_15 (.D(multiplexer_15_out), .clk(clk), .Q(out_6[4]));
  Multiplexer #(.select(2), .enable("false")) multiplexer_17 (
    .in0(Input[3]), .in1(out_6[3]), .in2(in_2), .in3(in_2), .out(multiplexer_17_out),
    .sel({clear, not_1_out[0]}));
  d_flip_flop d_flip_flop_16 (.D(multiplexer_16_out), .clk(clk), .Q(out_6[7]));
  d_flip_flop d_flip_flop_17 (.D(multiplexer_17_out), .clk(clk), .Q(out_6[3]));
  Multiplexer #(.select(2), .enable("false")) multiplexer_18 (
    .in0(Input[2]), .in1(out_6[2]), .in2(in_2), .in3(in_2), .out(multiplexer_18_out),
    .sel({clear, not_1_out[0]}));
  d_flip_flop d_flip_flop_18 (.D(multiplexer_18_out), .clk(clk), .Q(out_6[2]));
  Multiplexer #(.select(2), .enable("false")) multiplexer_19 (
    .in0(Input[1]), .in1(out_6[1]), .in2(in_2), .in3(in_2), .out(multiplexer_19_out),
    .sel({clear, not_1_out[0]}));
  d_flip_flop d_flip_flop_19 (.D(multiplexer_19_out), .clk(clk), .Q(out_6[1]));
  Multiplexer #(.select(2), .enable("false")) multiplexer_20 (
    .in0(Input[0]), .in1(out_6[0]), .in2(in_2), .in3(in_2), .out(multiplexer_20_out),
    .sel({clear, not_1_out[0]}));
  d_flip_flop d_flip_flop_20 (.D(multiplexer_20_out), .clk(clk), .Q(out_6[0]));
endmodule

module d_flip_flop (
  input  D,
  input  clk,
  output Q
);

  wire d_latch_1_q, not_1_out;

  d_latch d_latch_1 (.D(D), .c(not_1_out), .Q(d_latch_1_q));
  not not_1 (not_1_out, clk);
  d_latch d_latch_2 (.D(d_latch_1_q), .c(clk), .Q(Q));
endmodule

module d_latch (
  input  D,
  input  c,
  output Q
);

  wire and_1_out, and_2_out, half_adder_1_c_out, half_adder_1_sum, multiplexer_1_out, nand_1_out, nor_1_out,
       not_1_out, register_1_q;

  not not_1 (not_1_out, D);
  half_adder half_adder_1 (.A(c), .B(register_1_q), .sum(half_adder_1_sum), .c_out(half_adder_1_c_out));
  and and_1 (and_1_out, D, c);
  and and_2 (and_2_out, c, not_1_out);
  Register #(.width(1)) register_1 (.D(nand_1_out), .en(1'b1), .Q(register_1_q), .clk(c));  // open: clr
  nand nand_1 (nand_1_out, half_adder_1_sum, half_adder_1_c_out);
  nor nor_1 (nor_1_out, and_1_out, Q);
  nor nor_2 (Q, multiplexer_1_out, and_2_out);
  Multiplexer #(.enable("false")) multiplexer_1 (
    .in0(1'b1), .in1(nor_1_out), .out(multiplexer_1_out), .sel(register_1_q));
endmodule

module Register_File (
  input  [19:0] Input_data,
  input  [3:0] write_source__register,
  input  Write_Enable,
  input  clck,
  input  clear,
  input  [3:0] Input_Reg1,
  input  [3:0] Input_Reg2,
  output [19:0] Register_1_Data,
  output [19:0] Register_2_Data
);

  wire and_1_out, and_2_out, and_3_out, and_4_out, and_5_out, and_6_out, and_7_out, and_8_out, and_9_out,
       and_10_out, and_11_out, and_12_out, and_13_out, and_14_out, and_15_out, and_16_out, decoder_1_out0,
       decoder_1_out1, decoder_1_out2, decoder_1_out3, decoder_1_out4, decoder_1_out5, decoder_1_out6,
       decoder_1_out7, decoder_1_out8, decoder_1_out9, decoder_1_out10, decoder_1_out11, decoder_1_out12,
       decoder_1_out13, decoder_1_out14, decoder_1_out15;
  wire [19:0] n20_bit_register_1_out_6, n20_bit_register_2_out_6, n20_bit_register_3_out_6,
       n20_bit_register_4_out_6, n20_bit_register_5_out_6, n20_bit_register_6_out_6,
       n20_bit_register_7_out_6, n20_bit_register_8_out_6, n20_bit_register_9_out_6,
       n20_bit_register_10_out_6, n20_bit_register_11_out_6, n20_bit_register_12_out_6,
       n20_bit_register_13_out_6, n20_bit_register_14_out_6, n20_bit_register_15_out_6,
       n20_bit_register_16_out_6;

  Decoder #(.select(4)) decoder_1 (
    .out0(decoder_1_out0), .out1(decoder_1_out1), .out2(decoder_1_out2), .out3(decoder_1_out3),
    .out4(decoder_1_out4), .out5(decoder_1_out5), .out6(decoder_1_out6), .out7(decoder_1_out7),
    .out8(decoder_1_out8), .out9(decoder_1_out9), .out10(decoder_1_out10), .out11(decoder_1_out11),
    .out12(decoder_1_out12), .out13(decoder_1_out13), .out14(decoder_1_out14), .out15(decoder_1_out15),
    .sel(write_source__register));  // open: en
  and and_1 (and_1_out, decoder_1_out0, Write_Enable);
  and and_2 (and_2_out, decoder_1_out1, Write_Enable);
  and and_3 (and_3_out, decoder_1_out2, Write_Enable);
  and and_4 (and_4_out, decoder_1_out3, Write_Enable);
  and and_5 (and_5_out, decoder_1_out4, Write_Enable);
  and and_6 (and_6_out, decoder_1_out5, Write_Enable);
  and and_7 (and_7_out, decoder_1_out6, Write_Enable);
  and and_8 (and_8_out, decoder_1_out7, Write_Enable);
  and and_9 (and_9_out, decoder_1_out8, Write_Enable);
  and and_10 (and_10_out, decoder_1_out9, Write_Enable);
  and and_11 (and_11_out, decoder_1_out10, Write_Enable);
  and and_12 (and_12_out, decoder_1_out11, Write_Enable);
  and and_13 (and_13_out, decoder_1_out12, Write_Enable);
  and and_14 (and_14_out, decoder_1_out13, Write_Enable);
  and and_15 (and_15_out, decoder_1_out14, Write_Enable);
  and and_16 (and_16_out, decoder_1_out15, Write_Enable);
  _20_Bit_Register u_20_bit_register_1 (
    .in_2(and_1_out), .enable(clear), .clear(clck), .Input(Input_data), .out_6(n20_bit_register_1_out_6));  // open: clk
  _20_Bit_Register u_20_bit_register_2 (
    .in_2(and_2_out), .enable(clear), .clear(clck), .Input(Input_data), .out_6(n20_bit_register_2_out_6));  // open: clk
  _20_Bit_Register u_20_bit_register_3 (
    .in_2(and_3_out), .enable(clear), .clear(clck), .Input(Input_data), .out_6(n20_bit_register_3_out_6));  // open: clk
  _20_Bit_Register u_20_bit_register_4 (
    .in_2(and_4_out), .enable(clear), .clear(clck), .Input(Input_data), .out_6(n20_bit_register_4_out_6));  // open: clk
  _20_Bit_Register u_20_bit_register_5 (
    .in_2(and_5_out), .enable(clear), .clear(clck), .Input(Input_data), .out_6(n20_bit_register_5_out_6));  // open: clk
  _20_Bit_Register u_20_bit_register_6 (
    .in_2(and_6_out), .enable(clear), .clear(clck), .Input(Input_data), .out_6(n20_bit_register_6_out_6));  // open: clk
  _20_Bit_Register u_20_bit_register_7 (
    .in_2(and_7_out), .enable(clear), .clear(clck), .Input(Input_data), .out_6(n20_bit_register_7_out_6));  // open: clk
  _20_Bit_Register u_20_bit_register_8 (
    .in_2(and_8_out), .enable(clear), .clear(clck), .Input(Input_data), .out_6(n20_bit_register_8_out_6));  // open: clk
  _20_Bit_Register u_20_bit_register_9 (
    .in_2(and_9_out), .enable(clear), .clear(clck), .Input(Input_data), .out_6(n20_bit_register_9_out_6));  // open: clk
  _20_Bit_Register u_20_bit_register_10 (
    .in_2(and_10_out), .enable(clear), .clear(clck), .Input(Input_data), .out_6(n20_bit_register_10_out_6));  // open: clk
  _20_Bit_Register u_20_bit_register_11 (
    .in_2(and_11_out), .enable(clear), .clear(clck), .Input(Input_data), .out_6(n20_bit_register_11_out_6));  // open: clk
  _20_Bit_Register u_20_bit_register_12 (
    .in_2(and_12_out), .enable(clear), .clear(clck), .Input(Input_data), .out_6(n20_bit_register_12_out_6));  // open: clk
  _20_Bit_Register u_20_bit_register_13 (
    .in_2(and_13_out), .enable(clear), .clear(clck), .Input(Input_data), .out_6(n20_bit_register_13_out_6));  // open: clk
  _20_Bit_Register u_20_bit_register_14 (
    .in_2(and_14_out), .enable(clear), .clear(clck), .Input(Input_data), .out_6(n20_bit_register_14_out_6));  // open: clk
  _20_Bit_Register u_20_bit_register_15 (
    .in_2(and_15_out), .enable(clear), .clear(clck), .Input(Input_data), .out_6(n20_bit_register_15_out_6));  // open: clk
  _20_Bit_Register u_20_bit_register_16 (
    .in_2(and_16_out), .enable(clear), .clear(clck), .Input(Input_data), .out_6(n20_bit_register_16_out_6));  // open: clk
  Multiplexer #(.select(4), .width(20), .enable("false")) multiplexer_1 (
    .in0(n20_bit_register_1_out_6), .in1(n20_bit_register_2_out_6), .in2(n20_bit_register_3_out_6),
    .in3(n20_bit_register_4_out_6), .in4(n20_bit_register_5_out_6), .in5(n20_bit_register_6_out_6),
    .in6(n20_bit_register_7_out_6), .in7(n20_bit_register_8_out_6), .in8(n20_bit_register_9_out_6),
    .in9(n20_bit_register_10_out_6), .in10(n20_bit_register_11_out_6), .in11(n20_bit_register_12_out_6),
    .in12(n20_bit_register_13_out_6), .in13(n20_bit_register_14_out_6), .in14(n20_bit_register_15_out_6),
    .in15(n20_bit_register_16_out_6), .out(Register_1_Data), .sel(Input_Reg1));
  Multiplexer #(.select(4), .width(20), .enable("false")) multiplexer_2 (
    .in0(n20_bit_register_1_out_6), .in1(n20_bit_register_2_out_6), .in2(n20_bit_register_3_out_6),
    .in3(n20_bit_register_4_out_6), .in4(n20_bit_register_5_out_6), .in5(n20_bit_register_6_out_6),
    .in6(n20_bit_register_8_out_6), .in7(n20_bit_register_9_out_6), .in8(n20_bit_register_10_out_6),
    .in9(n20_bit_register_11_out_6), .in10(n20_bit_register_12_out_6), .in11(n20_bit_register_13_out_6),
    .in12(n20_bit_register_14_out_6), .in13(n20_bit_register_15_out_6), .in14(n20_bit_register_16_out_6),
    .out(Register_2_Data), .sel(Input_Reg2));  // open: in15
endmodule

module ProgramCounter (
  input  Next,
  input  Jump,
  input  Clock,
  input  [19:0] Input,
  input  Reset,
  input  [19:0] Value_To_Load
);

  wire [19:0] OUTPUT;

  _20_Bit_Adder u_20_bit_adder_1 (.C_in(1'b0), .A(OUTPUT), .B(Input), .Sum(Value_To_Load));  // open: C_Out
  Counter #(.width(20), .max('hfffff)) counter_1 (
    .load(Jump), .D(Value_To_Load), .count(Next), .Q(OUTPUT), .clk(Clock), .clr(Reset));  // open: carry

  // Other names for the same wires on the sheet: Clk = Clock; Count = Next; LoadEnable = Jump;
  //   ValueToLoad[19:0] = Value_To_Load
endmodule

module comparator (
  input  A,
  input  B,
  output out_3
);

  wire and_1_out, and_2_out, not_1_out, not_2_out;

  not not_1 (not_1_out, A);
  not not_2 (not_2_out, B);
  and and_1 (and_1_out, A, B);
  and and_2 (and_2_out, not_1_out, not_2_out);
  or or_1 (out_3, and_1_out, and_2_out);
endmodule

module _4_Bit_Comparator (
  input  [3:0] A,
  input  [3:0] B,
  output Equal
);

  wire comparator_1_out_3, comparator_2_out_3, comparator_3_out_3, comparator_4_out_3;

  comparator comparator_1 (.A(A[0]), .B(B[0]), .out_3(comparator_1_out_3));
  comparator comparator_2 (.A(A[1]), .B(B[1]), .out_3(comparator_2_out_3));
  comparator comparator_3 (.A(A[2]), .B(B[2]), .out_3(comparator_3_out_3));
  comparator comparator_4 (.A(A[3]), .B(B[3]), .out_3(comparator_4_out_3));
  and and_1 (Equal, comparator_1_out_3, comparator_2_out_3, comparator_3_out_3, comparator_4_out_3);
endmodule

module _20_Bit_Comparator (
  input  [19:0] in_1,
  input  [19:0] in_2,
  output eq
);

  wire n4_bit_comparator_1_equal, n4_bit_comparator_2_equal, n4_bit_comparator_3_equal,
       n4_bit_comparator_4_equal, n4_bit_comparator_5_equal;

  _4_Bit_Comparator u_4_bit_comparator_1 (.A(in_1[19:16]), .B(in_2[19:16]), .Equal(n4_bit_comparator_1_equal));
  _4_Bit_Comparator u_4_bit_comparator_2 (.A(in_1[15:12]), .B(in_2[15:12]), .Equal(n4_bit_comparator_2_equal));
  _4_Bit_Comparator u_4_bit_comparator_3 (.A(in_1[11:8]), .B(in_2[11:8]), .Equal(n4_bit_comparator_3_equal));
  _4_Bit_Comparator u_4_bit_comparator_4 (.A(in_1[7:4]), .B(in_2[7:4]), .Equal(n4_bit_comparator_4_equal));
  _4_Bit_Comparator u_4_bit_comparator_5 (.A(in_1[3:0]), .B(in_2[3:0]), .Equal(n4_bit_comparator_5_equal));
  and and_1 (eq, n4_bit_comparator_5_equal, n4_bit_comparator_4_equal, n4_bit_comparator_3_equal, n4_bit_comparator_2_equal, n4_bit_comparator_1_equal);
endmodule
